# Fritzing sketch ax350-driver-v2 (saved by Fritzing 0.9.3b)
circuit board: 6.7cm x 5.1cm
breadboards: 1

parts:
  MUX2 = SparkFun-74HC4051-8-Channel-Mux-Breakout [part_number=BOB-13906]
  MUX1 = SparkFun-74HC4051-8-Channel-Mux-Breakout [part_number=BOB-13906]
  ProMicro = SparkFun Pro Micro [part_number=DEV-12640]
  MX1-01 = female pin header, 2 pins [form="♀ (female)"]
  MX1-23 = female pin header, 2 pins [form="♀ (female)"]
  MX1-45 = female pin header, 2 pins [form="♀ (female)"]
  MX1-67 = female pin header, 2 pins [form="♀ (female)"]
  MX2-01 = female pin header, 2 pins [form="♀ (female)"]
  MX2-23 = female pin header, 2 pins [form="♀ (female)"]
  MX2-45 = female pin header, 2 pins [form="♀ (female)"]
  MX2-67 = female pin header, 2 pins [form="♀ (female)"]
  POW = female pin header, 2 pins [form="♀ (female)"]
  TXRX = female pin header, 2 pins [form="♀ (female)"]
  RAW = female pin header, 2 pins [form="♀ (female)"]

nets:
  N1: MUX2.Y7, MX2-67.pin2
  N2: MUX2.Y6, MX2-67.pin1
  N3: MUX2.Y5, MX2-45.pin2
  N4: MUX2.Y4, MX2-45.pin1
  N5: MUX2.Y3, MX2-23.pin2
  N6: MUX2.Y2, MX2-23.pin1
  N7: MUX2.Y1, MX2-01.pin2
  N8: MUX2.Y0, MX2-01.pin1
  GND: MUX2.GND, MUX1.GND, ProMicro.GND, POW.pin2, RAW.pin2
  VCC: MUX2.VCC, MUX1.VCC, ProMicro.VCC, POW.pin1
  N9: MUX2.!E!, ProMicro.D9
  N10: MUX2.S2, ProMicro.D8
  N11: MUX2.S1, ProMicro.D7
  N12: MUX2.S0, ProMicro.D6
  N13: MUX2.Z, MUX1.Z
  N14: MUX1.Y7, MX1-67.pin2
  N15: MUX1.Y6, MX1-67.pin1
  N16: MUX1.Y5, MX1-45.pin2
  N17: MUX1.Y4, MX1-45.pin1
  N18: MUX1.Y3, MX1-23.pin2
  N19: MUX1.Y2, MX1-23.pin1
  N20: MUX1.Y1, MX1-01.pin2
  N21: MUX1.Y0, MX1-01.pin1
  N22: MUX1.!E!, ProMicro.D5
  N23: MUX1.S2, ProMicro.D4
  N24: MUX1.S1, ProMicro.D3
  N25: MUX1.S0, ProMicro.D2
  N26: ProMicro.RAW, RAW.pin1
  N27: ProMicro.RXI, TXRX.pin2
  N28: ProMicro.TXO, TXRX.pin1

notes:
  AX350 Driver Board
  David Senk 2017
  REV 2
  0 1
  2 3
  4 5
  6 7
  MUX1
  MUX2
  https://senk.me/
  https://github.com/davidsenk/ax350-driver
  G

custom parts:
  SparkFun Pro Micro: This tiny little board does all of the neat-o Arduino tricks that you’re familiar with: 4 channels of 10-bit ADC, 5 PWM pins, 12 DIOs as well as hardware serial connections Rx and Tx. Running at 16MHz and 5V, this board will remind you a lot of your other favorite Arduino-compatible boards but this little guy can go just about anywhere. There is a voltage regulator on board so it can accept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
